# Fritzing sketch capacitor-circuit (saved by Fritzing 0.9.3b)
breadboards: 1

parts:
  R = Resistor [tolerance=±5% resistance=220 package=THT]
  Vin = AC Power [voltage=5 frequency=60]
  C = Ceramic Capacitor [capacitance=100nF package="100 mil [THT, multilayer]"]

nets:
  N1: R.Pin_0, Vin.V+
  N2: R.Pin_1, C.1
  GND: Vin.V-, C.0

notes:
  V0
  V1
