# Fritzing sketch capacitor-pdivide (saved by Fritzing 0.9.3b)
breadboards: 1

parts:
  R1 = Resistor [tolerance=±5% resistance=220 package=THT]
  C1 = Ceramic Capacitor [capacitance=100nF package="100 mil [THT, multilayer]"]
  Vi = AC Power [voltage=5 frequency=60]
  VC = Microphone

nets:
  N1: R1.Pin_0, Vi.V+
  N2: R1.Pin_1, C1.1, VC.pin1
  GND: C1.0, Vi.V-, VC.pin2
