# Fritzing sketch communication (saved by Fritzing 0.9.3b)
breadboards: 1

parts:
  Slave = Arduino Uno (Rev3)
  Master = Arduino Uno (Rev3)
  LED1 = smd LED [color="Red (635nm)" package="0603 [SMD]"]
  R1 = Resistor [tolerance=±5% resistance=220 package="0402 [SMD]"]

nets:
  N1: Slave.A4/SDA, Master.A4/SDA
  N2: Slave.A5/SCL, Master.A5/SCL
  N3: Slave.D13/SCK, LED1.anode
  GND: Slave.GND, Master.GND, R1.Pin_0
  N4: LED1.cathode, R1.Pin_1
