# Fritzing sketch inductor-circuit (saved by Fritzing 0.9.3b)
breadboards: 1

parts:
  R = Resistor [tolerance=±5% resistance=220 package=THT]
  Vin = AC Power [voltage=5 frequency=60]
  L = Inductor [package="400 mil [THT]"]

nets:
  N1: R.Pin_0, Vin.V+
  N2: R.Pin_1, L.pin_0
  GND: Vin.V-, L.pin_1

notes:
  V0
  V1
