# Fritzing sketch inductor-pdivide (saved by Fritzing 0.9.3b)
breadboards: 1

parts:
  R1 = Resistor [tolerance=±5% resistance=220 package=THT]
  Vi = AC Power [voltage=5 frequency=60]
  VL = Microphone
  L1 = Inductor [package="400 mil [THT]"]

nets:
  N1: R1.Pin_0, Vi.V+
  N2: R1.Pin_1, VL.pin1, L1.pin_0
  N3: Vi.V-, L1.pin_1
  GND: VL.pin2
