# Fritzing sketch low-pass-filter (saved by Fritzing 0.9.3b)
breadboards: 1

parts:
  R1 = Resistor [tolerance=±5% resistance=220 package=THT]
  C1 = Ceramic Capacitor [capacitance=100nF package="100 mil [THT, multilayer]"]
  Vin = AC Power [voltage=5 frequency=60]
  Vout = Microphone

nets:
  N1: R1.Pin_0, Vin.V+
  N2: R1.Pin_1, C1.1, Vout.pin1
  GND: C1.0, Vin.V-, Vout.pin2
