# Fritzing sketch parallel-resistors (saved by Fritzing 0.9.3b)

parts:
  R1 = Resistor [tolerance=±5% resistance=220 package=THT]
  Vin = AC Power [voltage=5 frequency=60]
  R2 = Resistor [tolerance=±5% resistance=220 package=THT]

nets:
  N1: R1.Pin_0, Vin.V+, R2.Pin_0
  N2: R1.Pin_1, Vin.V-, R2.Pin_1
