# Fritzing sketch rlc-pdivide (saved by Fritzing 0.9.3b)
breadboards: 1

parts:
  R1 = Resistor [tolerance=±5% resistance=220 package=THT]
  Vi = AC Power [voltage=5 frequency=60]
  VLC = Microphone
  L1 = Inductor [package="400 mil [THT]"]
  R2 = Resistor [tolerance=±5% resistance=220 package=THT]
  C1 = Ceramic Capacitor [capacitance=100nF package="100 mil [THT, multilayer]"]

nets:
  N1: R1.Pin_0, Vi.V+
  N2: R1.Pin_1, VLC.pin1, R2.Pin_0
  GND: Vi.V-
  N3: VLC.pin2, C1.0
  N4: L1.pin_0, R2.Pin_1
  N5: L1.pin_1, C1.1
