# Fritzing sketch series-resistors (saved by Fritzing 0.9.3b)

parts:
  R1 = Resistor [tolerance=±5% resistance=220 package=THT]
  Vm = AC Power [voltage=5 frequency=60]
  R2 = Resistor [tolerance=±5% resistance=220 package=THT]
  Vo = Microphone

nets:
  N1: R1.Pin_0, Vm.V+
  N2: R1.Pin_1, R2.Pin_0, Vo.pin1
  N3: Vm.V-, R2.Pin_1, Vo.pin2

notes:
  Vout
